# Fritzing sketch Six Light Signal Controller ver_1.3 (saved by Fritzing 1.0.3b)
circuit board: 6.4cm x 6cm
breadboards: 1

parts:
  TX1 = mystery part, 15 pins [chip_label=?]
  D13 = mystery part, 15 pins [chip_label=?]
  R1 = Resistor [tolerance=±5% power=0.25W resistance=220 package=THT]
  R2 = Resistor [tolerance=±5% power=0.25W resistance=220 package=THT]
  R3 = Resistor [tolerance=±5% power=0.25W resistance=220 package=THT]
  CC_|_CA = Toggle Switch [package=THT]
  R4 = Resistor [tolerance=±5% power=0.25W resistance=220 package=THT]
  R5 = Resistor [tolerance=±5% power=0.25W resistance=220 package=THT]
  R6 = Resistor [tolerance=±5% power=0.25W resistance=220 package=THT]
  Grn_PB1 = mystery part, 2 pins [chip_label=?]
  Signal = mystery part, 8 pins [chip_label=?]
  Rotary_Switch = mystery part, 4 pins [chip_label=?]

nets:
  N1: TX1.pin1, Rotary_Switch.pin1
  N2: TX1.pin2, Rotary_Switch.pin2
  N3: TX1.pin3, Rotary_Switch.pin3
  N4: TX1.pin4, Rotary_Switch.pin4
  N5: TX1.pin6, R6.Pin_0
  N6: TX1.pin7, R5.Pin_0
  N7: TX1.pin8, R4.Pin_0
  N8: TX1.pin9, R3.Pin_0
  N9: TX1.pin10, R2.Pin_0
  N10: TX1.pin11, R1.Pin_0
  N11: D13.pin12, CC_|_CA.L1
  N12: D13.pin14, CC_|_CA.L2, Grn_PB1.pin2
  N13: D13.pin15, Grn_PB1.pin1
  N14: R1.Pin_1, Signal.pin2
  N15: R2.Pin_1, Signal.pin3
  N16: R3.Pin_1, Signal.pin4
  N17: CC_|_CA.COM, Signal.pin1, Signal.pin8
  N18: R4.Pin_1, Signal.pin5
  N19: R5.Pin_1, Signal.pin6
  N20: R6.Pin_1, Signal.pin7

notes:
  Grn
  Ylw
  Red
  CMN
  Six Light Signal
  Controller ver 1.3
  +12V
  GND
  Arduino Nano
  CLEAR
  APPMED
  APPR
  STOP
  Connector
  End
