# Fritzing sketch Three Aspect Signal Controller v1.0 (saved by Fritzing 1.0.3b)
circuit board: 4.39818cm x 3.3cm
breadboards: 1

parts:
  R1 = Resistor [tolerance=±5% power=0.25W resistance=220 package=THT]
  R2 = Resistor [tolerance=±5% power=0.25W resistance=220 package=THT]
  Power = mystery part, 2 pins [chip_label=?]
  U1 = mystery part, 3 pins [chip_label=?]
  DPDT = mystery part, 3 pins [chip_label=?]
  Rotary_Switch = mystery part, 4 pins [chip_label=?]
  Signal = mystery part, 4 pins [chip_label=?]
  R3 = Resistor [tolerance=±5% power=0.25W resistance=220 package=THT]

nets:
  N1: R1.Pin_0, Signal.pin2
  N2: R1.Pin_1, Rotary_Switch.pin2
  N3: R2.Pin_0, Signal.pin3
  N4: R2.Pin_1, Rotary_Switch.pin3
  N5: Power.pin1, U1.pin3, DPDT.pin1
  N6: Power.pin2, U1.pin1, DPDT.pin3
  N7: U1.pin2, Signal.pin1
  N8: DPDT.pin2, Rotary_Switch.pin1
  N9: Rotary_Switch.pin4, R3.Pin_1
  N10: Signal.pin4, R3.Pin_0

notes:
  Three Aspect Signal
  Controller ver 1.0
  POS
  GND
  CMN
  Red
  Grn
  CA | CC
  Ylw
